# Fritzing sketch DC motors and sensor example wiring (saved by Fritzing 0.9.3b)
breadboards: 1

parts:
  Part2 = Arduino Uno (Rev3)
  M1 = DC Motor
  M2 = DC Motor
  VCC1 = Battery  # not connected
  HC-SR04_Sensor_1 = HC-SR04 Ultrasonic Distance Sensor
  Q1 = TRANSISTOR_NPN [package=to-92-ammo]
  R1 = Resistor [tolerance=±5% resistance=220 package="1206 [SMD]"]
  D1 = Diode [package=diode-1n4001]

nets:
  N1: Part2.D11_PWM/MOSI, HC-SR04_Sensor_1.TRIG
  N2: Part2.D12/MISO, HC-SR04_Sensor_1.ECHO
  N3: Part2.D3_PWM, R1.Pin_1
  5V: Part2.5V, M1.pin_1, M2.pin_1, HC-SR04_Sensor_1.VCC, D1.C
  GND: Part2.GND, HC-SR04_Sensor_1.GND, Q1.E
  N4: M1.pin_2, M2.pin_2, Q1.C
  N5: Q1.B, R1.Pin_0
